# Fritzing sketch MedicineAlarm (saved by Fritzing 0.8.5b)
circuit board: 7.85918cm x 5.79321cm
breadboards: 1

parts:
  Part1 = Arduino Uno (Rev3)
  J1 = Piezo Speaker
  U1 = LIPO-1000mAh [package=lipo-1000]

nets:
  N1: Part1.D12/MISO, J1.pin2
  N2: Part1.GND, J1.pin1, U1.-
  N3: Part1.5V, U1.+

notes:
  Actually the battery connects to the USB, but I did it this way so the schematic would work.
